# Fritzing sketch L293D (saved by Fritzing 0.6.3b)
breadboards: 1

parts:
  U1 = Voltage Regulator - 5V [package="TO220 [THT]"]
  C1 = Electrolytic Capacitor [capacitance=1µF package="100 mil [THT, electrolytic]"]
  C2 = Electrolytic Capacitor [capacitance=1µF package="100 mil [THT, electrolytic]"]
  C3 = Ceramic Capacitor [capacitance=10pF package="100 mil [THT, multilayer]"]
  IC1 = IC, DIP package, 16 pins [chip_label=L293D spacing=300mil]
  Arduino1 = Arduino
  M1 = DC Motor
  VCC1 = Battery block 9V

nets:
  N1: U1.input_voltage, C1.+, VCC1.+
  N2: U1.GND, C1.-, C2.-, C3.0, IC1.pin4, IC1.pin5, IC1.pin12, IC1.pin13, VCC1.-
  N3: U1.output_voltage, C2.+, C3.1, IC1.pin8, IC1.pin16
  N4: IC1.pin1, Arduino1.D9
  N5: IC1.pin2, Arduino1.D4
  N6: IC1.pin3, M1.pin_1
  N7: IC1.pin6, M1.pin_2
  N8: IC1.pin7, Arduino1.D3
