# Fritzing sketch MotorControl (saved by Fritzing 0.9.0b)
circuit board: 5.97359cm x 4.50848cm
breadboards: 1

parts:
  IC1 = L293D [package=THT]
  Part1 = Arduino Yun
  J1 = Screw terminal - 2 pins [package=THT]
  J2 = Power Jack [package=power_jack_slot]

nets:
  N1: IC1.Enable_1, IC1.+Vmotor, IC1.Enable_2, IC1.+V, J2.PWR
  N2: IC1.In_1, IC1.In_2, Part1.D8
  N3: IC1.Out_1_(_Controlled_by_Enable_1_), IC1.Out_2_(_Controlled_by_Enable_1_), J1.pin2
  GND: IC1.0V, Part1.GND, J2.GNDBREAK, J2.GND
  N4: IC1.In_3, IC1.In_4, Part1.D7
  N5: IC1.Out_3_(_Controlled_by_Enable_2_), IC1.Out_4_(_Controlled_by_Enable_2_), J1.pin1
