# Fritzing sketch Sketch (saved by Fritzing 0.9.0b)
circuit board: 4.48376cm x 5.39703cm
breadboards: 1

parts:
  J2 = female pin header, 2 pins [form="♀ (female)"]
  M1 = DC Motor [part_number=RS-360SH]
  R5 = Resistor [tolerance=±5% resistance=220 package=THT]
  R6 = Resistor [tolerance=±5% resistance=330k package=THT]
  R2 = Resistor [tolerance=±5% resistance=10k package=THT]
  K1 = Relay [part_number=N4078-2C-6V-0.36W package=THT]
  R3 = Resistor [tolerance=±5% resistance=10k package=THT]
  J1 = Power Jack [part_number="Power Supply" package=power_jack_pth_lock]
  R7 = Resistor [tolerance=±5% resistance=220 package=THT]
  U1 = Optocoupler [package=THT]
  R4 = Resistor [tolerance=±5% resistance=220 package=THT]
  Part1 = Arduino Yun [part_number="Arduino Yun"]
  Q2 = NPN-Transistor [package="TO92 [THT]"]
  R8 = Resistor [tolerance=±5% resistance=330k package=THT]

nets (from the schematic view):
  N1: J2.pin1, R2.Pin_1
  N2: J2.pin2, R6.Pin_0, Q2.B
  N3: M1.pin_1, K1.B
  N4: M1.pin_2, K1.COIL2, J1.GND, J1.GNDBREAK
  N5: R5.Pin_0, R3.Pin_0, Part1.5V
  N6: R5.Pin_1, R4.Pin_0
  N7: R6.Pin_1, U1.Pin_2, Part1.GND, Q2.E
  N8: R2.Pin_0, R3.Pin_1
  N9: K1.COIL1, U1.Pin_4
  N10: K1.C1, K1.C2, J1.PWR, U1.Pin_5, R8.Pin_0
  N11: R7.Pin_0, Part1.ICSP_MISO, Part1.D12/MISO
  N12: R7.Pin_1, U1.Pin_1
  N13: U1.Pin_6, R8.Pin_1
  N14: R4.Pin_1, Part1.D2, Q2.C

notes:
  Sensore di livello Acqua
  Pompa dell Acqua
  PARTE ARDUINO [GND_ARDUINO, +5V]
  PARTE MOTORE [GND_ALIM, +6V]
